// Logisim project xor.circ as structural Verilog: 1 circuit, main circuit main
module main (
  input  x0,
  input  x1,
  output y0,
  output y1
);

  wire and_1_out, or_1_out;

  xor xor_1 (y0, x0, x1);
  or or_1 (or_1_out, x1, x0);
  and and_1 (and_1_out, x1, x0);
  and and_2 (y1, or_1_out, ~and_1_out);  // AND_Gate
endmodule
